# Fritzing sketch Motor Test Sketch (saved by Fritzing 0.9.3b)
circuit board: 17.9cm x 8.63842cm
breadboards: 1

parts:
  U3 = atmega328 [package=dip]
  R17 = Resistor [tolerance=±5% resistance=10k package=THT]
  J58 = rounded female pin header, 3 pins [form="♀ (female rounded)"]
  XTAL = Crystal [frequency="16 Mhz" package=THT]
  R2 = Resistor [tolerance=±5% resistance=100k package=THT]
  R15 = Resistor [tolerance=±5% resistance=1k package=THT]
  Q2 = NPN-Transistor [package="TO92 [THT]"]
  C6 = Ceramic Capacitor [capacitance=22pF package="100 mil [THT, multilayer]"]
  C5 = Ceramic Capacitor [capacitance=22pF package="100 mil [THT, multilayer]"]
  - = screw terminal, 2 pins
  C7 = Ceramic Capacitor [capacitance="100 nF" package="100 mil [THT, multilayer]"]
  C10 = Electrolytic Capacitor [capacitance=33µF voltage=25V package="100 mil [THT, electrolytic]"]
  R14 = Resistor [tolerance=±5% resistance=1k package=THT]
  R16 = Resistor [tolerance=±5% resistance=1k package=THT]
  C9 = Ceramic Capacitor [capacitance="100 nF" package="100 mil [THT, multilayer]"]
  C8 = Ceramic Capacitor [capacitance="100 nF" package="100 mil [THT, multilayer]"]
  Q10 = MOSFET-NCHANNEL [package=sot23-3]
  R25 = Resistor [tolerance=±5% resistance=56k package=THT]
  R29 = Resistor [tolerance=±5% resistance=56k package=THT]
  R24 = Resistor [tolerance=±5% resistance=56k package=THT]
  R28 = Resistor [tolerance=±5% resistance=22k package=THT]
  D7 = Diode [package=diode-1n4001]
  SIM800L_20MM1 = SIM800L_20MM
  Q7 = Sharp PC817 [package=THT]
  J48 = rounded female pin header, 2 pins [form="♀ (female rounded)"]
  RESET1 = Pushbutton [package="[THT]"]
  J60 = Rectifier_6A [package=THT]
  J72 = 4pth XH JST CUSTOM [form="♀ (female rounded)" package=THT]
  J73 = 4pth XH JST CUSTOM [form="♀ (female rounded)" package=THT]
  J77 = 2PTH JST FROM HEADER 5 [form="♀ (female rounded)" package=THT]
  C12 = Electrolytic Capacitor [capacitance=0.47mF voltage=10V package="200 mil [THT, electrolytic]"]
  D8 = Diode [package=diode-1n4001]
  D9 = Diode [package=diode-1n4001]
  R30 = Resistor [tolerance=±5% resistance=100k package=THT]
  C2 = Capacitor Polarized [package=cpol-radial-1000uf-25v]
  U8 = IC741 Op. Amp [part_number=IC741]
  R31 = Resistor [tolerance=±5% resistance=1k package=THT]
  R32 = Resistor [tolerance=±5% resistance=100k package=THT]
  R33 = Resistor [tolerance=±5% resistance=100k package=THT]
  Q11 = Sharp PC817 [package=THT]
  Q12 = NPN-Transistor [part_number=2N2222A package="TO92 [THT]"]
  R34 = Resistor [tolerance=±5% resistance=1k package=THT]
  R35 = Resistor [tolerance=±5% resistance=1k package=THT]
  Q13 = Sharp PC817 [package=THT]
  Q14 = NPN-Transistor [part_number=2N2222A package="TO92 [THT]"]
  R36 = Resistor [tolerance=±5% resistance=1k package=THT]
  J78 = 3pth XH JST Custom [form="♀ (female rounded)" package=THT]
  J79 = rounded female pin header, 2 pins [form="♀ (female rounded)"]
  J81 = 4pth XH JST CUSTOM [form="♀ (female rounded)" package=THT]
  R37 = Resistor [tolerance=±5% resistance=1k package=THT]
  LED1 = LED - 3mm [color="Red (633nm)" package="3 mm [THT]"]
  D11 = Diode [package=diode-1n4148]
  RL3 = OMRON PCB Power Relay – G5LE [part_number="G5LE-1\n" package=THT]
  RL4 = OMRON PCB Power Relay – G5LE [part_number="G5LE-1\n" package=THT]
  C_START_STOP = screw terminal, 3 pins
  D12 = Diode [package=diode-1n4148]
  R_B = screw terminal, 2 pins
  R38 = Resistor [tolerance=±5% resistance=10k package=THT]
  R_Y_B = screw terminal, 3 pins
  R39 = Resistor [tolerance=±5% resistance=10k package=THT]
  R40 = Resistor [tolerance=±5% resistance=10k package=THT]
  R41 = Resistor [tolerance=±5% resistance=10k package=THT]
  R42 = Resistor [tolerance=±5% resistance=10k package=THT]
  C14 = Capacitor [package=cap-pth-large]
  R43 = Resistor [tolerance=±5% resistance=10k package=THT]
  C15 = Capacitor [package=cap-pth-large]
  D13 = Diode [package=diode-1n4148]
  D14 = Diode [package=diode-1n4148]
  D15 = Diode [package=diode-1n4148]
  D16 = Diode [package=diode-1n4148]
  J83 = 3pth XH JST Custom [form="♀ (female rounded)" package=THT]
  S1 = Push Button Switch [package=os]
  J84 = 3pth XH JST Custom [form="♀ (female rounded)" package=THT]
  Step_Down_Module3 = MP1584 Step Down Module [part_number=MP1584]
  TP4056_Battery_Charge_Module3 = TP4056 Lithium Ion Battery Charger
  LM2596_Module2 = LM2596 Step Down Module
  Q16 = TL431 Transistor [package="TO92 [THT]"]
  Q17 = MOSFET-NCHANNEL [package=sot23-3]
  R44 = Resistor [tolerance=±5% resistance=100k package=THT]
  R45 = Resistor [tolerance=±5% resistance=100k package=THT]
  R46 = Resistor [tolerance=±5% resistance=100k package=THT]
  R47 = Resistor [tolerance=±5% resistance=100k package=THT]
  U9 = MOV [package=v18za2p]

nets:
  N1: U3.RESET, R17.Pin_1, RESET1.Pin_1, RESET1.Pin_2
  N2: U3.D0_(RX), J48.pin1
  N3: U3.D1_(TX), J48.pin2
  N4: U3.D2, R16.Pin_1
  N5: U3.D3_(PWM), R30.Pin_0
  N6: U3.D4, R15.Pin_1
  N7: U3.VCC, U3.AVCC, U3.AREF, R17.Pin_0, C7.1, C9.0, C8.1, SIM800L_20MM1.PIN2, C12.+, U8.V+, R32.Pin_1, Q11.Pin_4, Q13.Pin_4, R36.Pin_1, J78.pin3, J81.pin4, Q17.D
  N8: U3.GND, J58.pin3, Q2.E, C6.0, C5.1, C7.0, C10.-, C9.1, C8.0, SIM800L_20MM1.PIN_6, Q7.Pin_3, RESET1.Pin_3, RESET1.Pin_4, C12.-, U8.-V, R33.Pin_1, Q12.E, Q14.E, R37.Pin_0, Step_Down_Module3.OUT-, Q16.Anode, R44.Pin_1
  N9: U3.XLAT1, XTAL.pin_0, C5.0
  N10: U3.XLAT2, XTAL.pin_1, C6.1
  N11: U3.D5_(PWM), J58.pin1
  N12: U3.D6_(PWM), J58.pin2
  N13: U3.D9_(PWM), R31.Pin_0
  N14: U3.D10_(PWM), R14.Pin_0
  N15: U3.D12, Q13.Pin_2
  N16: U3.D13, Q11.Pin_2
  N17: U3.A2, J81.pin1
  N18: U3.A3, J81.pin2
  N19: U3.A4, J81.pin3
  N20: U3.A5, LED1.anode
  N21: R2.Pin_0, Step_Down_Module3.IN-, TP4056_Battery_Charge_Module3.IN-, LM2596_Module2.IN+
  N22: R2.Pin_1, Q10.G, Step_Down_Module3.IN+, TP4056_Battery_Charge_Module3.IN+, LM2596_Module2.IN-
  N23: R15.Pin_0, Q2.B
  N24: Q2.C, SIM800L_20MM1.PIN_8
  N25: -.pin1, J60.DC_-, C2.-, S1.C1, S1.C2, TP4056_Battery_Charge_Module3.B-, TP4056_Battery_Charge_Module3.OUT-
  N26: -.pin2, TP4056_Battery_Charge_Module3.B+
  N27: C10.+, R14.Pin_1, Q7.Pin_4
  N28: R16.Pin_0, SIM800L_20MM1.PIN_7
  N29: Q10.S, D9.C, Q17.S, R45.Pin_0, R46.Pin_0
  N30: Q10.D, TP4056_Battery_Charge_Module3.OUT+
  N31: R25.Pin_0, R_B.pin2
  N32: R25.Pin_1, R29.Pin_0, U9.P$2
  N33: R29.Pin_1, J72.pin3
  N34: R24.Pin_0, R_B.pin1
  N35: R24.Pin_1, D7.C, U9.P$1
  N36: R28.Pin_0, J72.pin4
  N37: R28.Pin_1, D7.A
  N38: SIM800L_20MM1.PIN_4, J79.pin2
  N39: SIM800L_20MM1.PIN_5, J79.pin1
  N40: Q7.Pin_1, J73.pin3
  N41: Q7.Pin_2, J73.pin4
  N42: J60.DC_+, D8.A, C2.+
  N43: J60.AC_IN#1, J77.pin2
  N44: J60.AC_IN#2, J77.pin1
  N45: J72.pin1, D14.A, D15.A
  N46: J72.pin2, D13.C, D16.C
  N47: J73.pin1, S1.NO1, S1.NO2, LM2596_Module2.OUT+
  N48: J73.pin2, U8.-IN
  N49: D8.C, LM2596_Module2.OUT-
  N50: D9.A, R30.Pin_1, Step_Down_Module3.OUT+
  N51: U8.+IN, R32.Pin_0, R33.Pin_0
  N52: U8.OUT, R31.Pin_1
  N53: Q11.Pin_1, Q13.Pin_1, R36.Pin_0
  N54: Q11.Pin_3, R34.Pin_1
  N55: Q12.B, R34.Pin_0
  N56: Q12.C, J78.pin1
  N57: R35.Pin_0, Q13.Pin_3
  N58: R35.Pin_1, Q14.B
  N59: Q14.C, J78.pin2
  N60: R37.Pin_1, LED1.cathode
  N61: D11.A, RL4.COIL1, J83.pin2
  N62: D11.C, RL3.COIL1, RL4.COIL2, D12.C, J83.pin1
  N63: RL3.C, RL4.C, C_START_STOP.pin1
  N64: RL3.COIL2, D12.A, J83.pin3
  N65: RL3.B, C_START_STOP.pin3
  N66: RL4.A, C_START_STOP.pin2
  N67: R38.Pin_0, R_Y_B.pin1, J84.pin3
  N68: R38.Pin_1, R39.Pin_1, D15.C, D16.A
  N69: R_Y_B.pin2, R39.Pin_0, C14.2, J84.pin1
  N70: R_Y_B.pin3, R40.Pin_0
  N71: R40.Pin_1, R41.Pin_0
  N72: R41.Pin_1, R42.Pin_0
  N73: R42.Pin_1, R43.Pin_1, C15.1
  N74: C14.1, C15.2
  N75: R43.Pin_0, D13.A, D14.C
  N76: Q16.Ref, R44.Pin_0, R45.Pin_1
  N77: Q16.Cathode, R46.Pin_1, R47.Pin_1
  N78: Q17.G, R47.Pin_0

notes:
  M-
  RX
  TX
  STX
  SRX
  1
  MOTOR
  FeedBack
  +
  Battery
  J1

custom parts:
  Rectifier_6A: stand Up rectifier 6A
  2PTH JST FROM HEADER 5: Generic rounded female header
  3pth XH JST Custom: 3PTH XH JST
  Push Button Switch: DPDT On/Off Switch, when pressed connects NO to C.
  MP1584 Step Down Module: Step Down Module based on MP1584
  TP4056 Lithium Ion Battery Charger: A lithium battery charging and powering shield.
  LM2596 Step Down Module: LM2596 Step Down Regulator
  TL431 Transistor: NPN transistor cum comporator cum voltage refence TL431/KA431
  MOV: Metal Oxide Varistor
